# Fritzing sketch Obstacle Sensing Schematic (saved by Fritzing 0.9.3b)
breadboards: 1

parts:
  Part1 = Arduino Uno (Rev3)
  DHT1 = DHT22 Humidity and Temperature Sensor
  hc-sr4 = hc-sr04
  hc-sr5 = hc-sr04
  hc-sr3 = hc-sr04

nets:
  N1: Part1.A0, DHT1.DATA
  N2: Part1.A1, hc-sr5.Trig, hc-sr5.Echo
  N3: Part1.A3, hc-sr4.Trig, hc-sr4.Echo
  N4: Part1.A5/SCL, hc-sr3.Trig, hc-sr3.Echo
  VCC: Part1.5V, DHT1.VDD, hc-sr4.VCC, hc-sr5.VCC, hc-sr3.VCC
  GND: Part1.GND, DHT1.GND, hc-sr4.GND, hc-sr5.GND, hc-sr3.GND
